# Fritzing sketch slotMachine (saved by Fritzing 0.9.3b)
breadboards: 1

parts:
  Bauteil1 = Arduino Mega ADK (Rev3)
  LCD1 = LCD screen
  S1 = Pushbutton [package="[THT]"]

nets:
  N1: Bauteil1.D21/SCL, LCD1.RS
  N2: Bauteil1.D20/SDA, LCD1.R/W
  GND: Bauteil1.GND, LCD1.VSS, S1.Pin_3, S1.Pin_4
  5V: Bauteil1.IOREF, Bauteil1.5V, LCD1.VDD
  N3: Bauteil1.D2_PWM, S1.Pin_1, S1.Pin_2

// code stored in the sketch: slotMachine.ino
void setup() {

}

void loop() {

}
